# Fritzing sketch wiring (saved by Fritzing 0.9.4)
breadboards: 1

parts:
  R1 = Resistor [tolerance=±5% resistance=4.7k package=THT]
  DS1 = DS18B20 1-Wire Temperature Sensor [part_number=DS18B20]
  U1 = NodeMCU V3.0
  microSD1 = MicroSD Card Module
  DHT1 = DHT11 Humitidy and Temperature Sensor
  R2 = Resistor [tolerance=±5% resistance=4.7k package=THT]

nets:
  N1: R1.Pin_0, DS1.DQ, U1.D2
  VDD: R1.Pin_1, DS1.VDD, U1.3V3, microSD1.VCC, DHT1.VDD, R2.Pin_1
  GND: DS1.GND, U1.GND, microSD1.GND, DHT1.GND
  N2: U1.D1, DHT1.DATA, R2.Pin_0
  N3: U1.D5, microSD1.SCK
  N4: U1.D6, microSD1.MISO
  N5: U1.D7, microSD1.MOSI
  N6: U1.D8, microSD1.CS

custom parts:
  NodeMCU V3.0: ESP8266 based NodeMCU
  DHT11 Humitidy and Temperature Sensor: DHT11 Humidity and Temperature Sensor
